# Fritzing sketch esp32_rf_receiver (saved by Fritzing 0.9.3b)
breadboards: 1

parts:
  U1 = RXB6 Superhetrodyne receiver [part_number=RXB6 package=sip]
  U2 = ESP32S-HiLetgo [part_number=ESP32S-HiLetgo]

nets:
  N1: U1.RFGND, U1.DGND, U2.GND
  N2: U1.RFVCC, U1.DVCC, U2.VIN
  N3: U1.DATA, U2.GPIO14

notes:
  antenna

custom parts:
  RXB6 Superhetrodyne receiver: RF Link receivers RXB6, 315, 433.92 Mhz (or custom) Converted from the Spartfun Rf-LINK_RX part (which doesn't apper to be quite correct).
  ESP32S-HiLetgo: HiLetgo ESP-WROOM-32 ESP32 ESP-32S Development Board 2.4GHz Dual-Mode WiFi + Bluetooth Dual Cores Microcontroller The ESP32 integrated with Antenna switches, RF Balun, power amplifiers, low-noise amplifiers, filters, and management modules, and the entire solution occupies the least area of PCB. 2.4 GHz Wi-Fi plus Bluetooth dual-mode chip, with TSMC Ultra-low power consumption 40nm technology,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
